# Fritzing sketch Esp01_dht_v1 (saved by Fritzing 0.9.4)
circuit board: 10cm x 5cm
breadboards: 1

parts:
  ESP-01 = ESP8266 WiFi Module [part_number=ESP8266]
  DHT1 = DHT11 Humitidy and Temperature Sensor
  C1 = Ceramic Capacitor [capacitance=100nF package="100 mil [THT, multilayer]"]
  Buck_Converter = RioRand LM2596
  MicroUSB = female pin header, 5 pins [form="♀ (female)"]
  R1 = Resistor [tolerance=±5% resistance=10k package=THT]
  R4 = Resistor [tolerance=±5% resistance=3.3 package=THT]
  R2 = Resistor [tolerance=±5% resistance=3.3 package=THT]
  R3 = Resistor [tolerance=±5% resistance=10k package=THT]

nets:
  N1: ESP-01.VCC, C1.1, Buck_Converter.Pin_3, R1.Pin_1, R4.Pin_0, R2.Pin_0, R3.Pin_0
  N2: ESP-01.GPIO_0, R4.Pin_1
  N3: ESP-01.GPIO_2, DHT1.DATA, R2.Pin_1
  N4: ESP-01.CH_PD, R3.Pin_1
  GND: ESP-01.GND, DHT1.GND, C1.0, Buck_Converter.Pin_4
  N5: DHT1.VDD, R1.Pin_0
  N6: Buck_Converter.Pin_1, MicroUSB.pin1
  N7: Buck_Converter.Pin_2, MicroUSB.pin5

custom parts:
  ESP8266 WiFi Module: Generic WiFi Module based on the ESP8266 with onboard PCB antenna and UART communications
  DHT11 Humitidy and Temperature Sensor: DHT11 Humidity and Temperature Sensor
